# Fritzing sketch Feeder_Fritzing (saved by Fritzing 1.0.6)
circuit board: 10.5cm x 8.3cm

parts:
  MH-ET_LIVE_ESP32_DEVKIT1 = MH-ET LIVE ESP32 DEVKIT 38 pins
  HC-SR04_Sensor_1 = HC-SR04 Ultrasonic Distance Sensor
  Composant2 = RFID-RC522-v2
  LED2 = RGB LED (com. cathode, rbg) [color="Red (633nm)" current=0.030A package="5 mm [THT]"]
  J2 = Basic Servo
  J4 = female pin header, 6 pins [form="♀ (female)"]
  J5 = female pin header, 4 pins [form="♀ (female)"]
  PIR1 = PIR sensor
  J10 = female pin header, 1 pin [form="♀ (female)"]
  J12 = female pin header, 1 pin [form="♀ (female)"]
  J18 = female pin header, 1 pin [form="♀ (female)"]
  J20 = female pin header, 1 pin [form="♀ (female)"]  # not connected
  J17 = female pin header, 1 pin [form="♀ (female)"]  # not connected
  J19 = female pin header, 1 pin [form="♀ (female)"]
  J1 = female pin header, 4 pins [form="♀ (female)"]

nets:
  3V3: MH-ET_LIVE_ESP32_DEVKIT1.3V3, Composant2.3.3V
  N1: MH-ET_LIVE_ESP32_DEVKIT1.IO32, HC-SR04_Sensor_1.TRIG
  N2: MH-ET_LIVE_ESP32_DEVKIT1.IO33, HC-SR04_Sensor_1.ECHO
  N3: MH-ET_LIVE_ESP32_DEVKIT1.IO25, LED2.red_anode
  N4: MH-ET_LIVE_ESP32_DEVKIT1.IO26, LED2.common_cathode
  N5: MH-ET_LIVE_ESP32_DEVKIT1.IO27, LED2.blue_anode
  N6: MH-ET_LIVE_ESP32_DEVKIT1.IO14, PIR1.SIG
  GND: MH-ET_LIVE_ESP32_DEVKIT1.GND#58, HC-SR04_Sensor_1.GND, J2.gnd, PIR1.GND
  N7: MH-ET_LIVE_ESP32_DEVKIT1.IO13, J2.pulse
  VCC: MH-ET_LIVE_ESP32_DEVKIT1.5V, HC-SR04_Sensor_1.VCC, J2.vcc, J5.pin1, PIR1.VDD
  N8: MH-ET_LIVE_ESP32_DEVKIT1.GND#64, J5.pin4
  N9: MH-ET_LIVE_ESP32_DEVKIT1.IO23, Composant2.MOSI, J10.pin1, J12.pin1
  N10: MH-ET_LIVE_ESP32_DEVKIT1.IO22, Composant2.RST
  N11: MH-ET_LIVE_ESP32_DEVKIT1.GND#70, Composant2.GND, LED2.green_anode
  N12: MH-ET_LIVE_ESP32_DEVKIT1.IO19, Composant2.MISO
  N13: MH-ET_LIVE_ESP32_DEVKIT1.IO18, Composant2.SCK
  N14: MH-ET_LIVE_ESP32_DEVKIT1.IO5, Composant2.SDA
  N15: MH-ET_LIVE_ESP32_DEVKIT1.IO17, J5.pin3
  N16: MH-ET_LIVE_ESP32_DEVKIT1.IO16, J5.pin2
  N17: J4.pin3, J1.pin1
  N18: J4.pin4, J1.pin2
  N19: J4.pin5, J1.pin3
  N20: J4.pin6, J1.pin4
  N21: J18.pin1, J19.pin1

custom parts:
  MH-ET LIVE ESP32 DEVKIT 38 pins: http://mh.nodebb.com/topic/2/mh-et-live-esp32-devkit
  RFID-RC522-v2: A simple China made RFID-RC522 Reader; do check the pin labels, as this is a MFRC522 based clone.
